// Logisim project Tarea2_Arqui.circ as structural Verilog: 10 circuits, main circuit main
module Suma (
  input  [15:0] in_1,
  output [7:0] out_2,
  output [7:0] out_3,
  output [7:0] out_4
);

  wire sumador_1_out_5, sumador_2_out_5, sumador_3_out_5, sumador_4_out_5, sumador_5_out_5, sumador_6_out_5,
       sumador_7_out_5;

  Sumador sumador_1 (.in_1(in_1[0]), .in_2(in_1[8]), .in_3(1'b0), .out_5(sumador_1_out_5), .out_4(out_4[0]));
  Sumador sumador_2 (.in_1(in_1[1]), .in_2(in_1[9]), .in_3(sumador_1_out_5), .out_5(sumador_2_out_5), .out_4(out_4[1]));
  Sumador sumador_3 (
    .in_1(in_1[2]), .in_2(in_1[10]), .in_3(sumador_2_out_5), .out_5(sumador_3_out_5), .out_4(out_4[2]));
  Sumador sumador_4 (
    .in_1(in_1[3]), .in_2(in_1[11]), .in_3(sumador_3_out_5), .out_5(sumador_4_out_5), .out_4(out_4[3]));
  Sumador sumador_5 (
    .in_1(in_1[4]), .in_2(in_1[12]), .in_3(sumador_4_out_5), .out_5(sumador_5_out_5), .out_4(out_4[4]));
  Sumador sumador_6 (
    .in_1(in_1[5]), .in_2(in_1[13]), .in_3(sumador_5_out_5), .out_5(sumador_6_out_5), .out_4(out_4[5]));
  Sumador sumador_7 (
    .in_1(in_1[6]), .in_2(in_1[14]), .in_3(sumador_6_out_5), .out_5(sumador_7_out_5), .out_4(out_4[6]));
  Sumador sumador_8 (.in_1(in_1[7]), .in_2(in_1[15]), .in_3(sumador_7_out_5), .out_4(out_4[7]));  // open: out_5

  assign out_2 = in_1[7:0];
  assign out_3 = in_1[15:8];
endmodule

module main (
  input  [2:0] in_1,
  input  [7:0] in_2,
  input  [7:0] in_3
);

  wire [7:0] and_1_out_4, multiplexer_1_out, nand_1_out_4, nor_1_out_4, or_1_out_4, resta_1_out_2,
       suma_1_out_4, xnor_1_out_4, xor_1_out_4;
  wire [15:0] demultiplexer_1_out0, demultiplexer_1_out1, demultiplexer_1_out2, demultiplexer_1_out3,
       demultiplexer_1_out4, demultiplexer_1_out5, demultiplexer_1_out6, demultiplexer_1_out7;

  Demultiplexer #(.select(3), .width(16)) demultiplexer_1 (
    .out0(demultiplexer_1_out0), .out1(demultiplexer_1_out1), .out2(demultiplexer_1_out2),
    .out3(demultiplexer_1_out3), .out4(demultiplexer_1_out4), .out5(demultiplexer_1_out5),
    .out6(demultiplexer_1_out6), .out7(demultiplexer_1_out7), .in({in_3, in_2}), .sel(in_1), .en(1'b1));
  Suma suma_1 (.in_1(demultiplexer_1_out0), .out_4(suma_1_out_4));  // open: out_2, out_3
  OR or_1 (.in_1(demultiplexer_1_out1), .out_4(or_1_out_4));  // open: out_2, out_3
  AND and_1 (.in_1(demultiplexer_1_out2), .out_4(and_1_out_4));  // open: out_2, out_3
  XOR xor_1 (.in_1(demultiplexer_1_out3), .out_4(xor_1_out_4));  // open: out_2, out_3
  Resta resta_1 (.in_1(demultiplexer_1_out4), .out_2(resta_1_out_2));  // open: out_3, out_4
  NOR nor_1 (.in_1(demultiplexer_1_out5), .out_4(nor_1_out_4));  // open: out_2, out_3
  NAND nand_1 (.in_1(demultiplexer_1_out6), .out_4(nand_1_out_4));  // open: out_2, out_3
  XNOR xnor_1 (.in_1(demultiplexer_1_out7), .out_4(xnor_1_out_4));  // open: out_2, out_3
  Multiplexer #(.select(3), .width(8)) multiplexer_1 (
    .in0(suma_1_out_4), .in1(or_1_out_4), .in2(and_1_out_4), .in3(xor_1_out_4), .in4(resta_1_out_2),
    .in5(nor_1_out_4), .in6(nand_1_out_4), .in7(xnor_1_out_4), .out(multiplexer_1_out), .sel(in_1), .en(1'b1));
  LED led_1 (.in(multiplexer_1_out[5]));
  LED led_2 (.in(multiplexer_1_out[6]));
  LED led_3 (.in(multiplexer_1_out[7]));
  LED led_4 (.in(multiplexer_1_out[3]));
  LED led_5 (.in(multiplexer_1_out[4]));
  LED led_6 (.in(multiplexer_1_out[0]));
  LED led_7 (.in(multiplexer_1_out[2]));
  LED led_8 (.in(multiplexer_1_out[1]));
endmodule

module OR (
  input  [15:0] in_1,
  output [7:0] out_2,
  output [7:0] out_3,
  output [7:0] out_4
);

  or or_1 (out_4[0], in_1[0], in_1[8]);
  or or_2 (out_4[1], in_1[1], in_1[9]);
  or or_3 (out_4[2], in_1[2], in_1[10]);
  or or_4 (out_4[3], in_1[3], in_1[11]);
  or or_5 (out_4[4], in_1[4], in_1[12]);
  or or_6 (out_4[5], in_1[5], in_1[13]);
  or or_7 (out_4[6], in_1[6], in_1[14]);
  or or_8 (out_4[7], in_1[7], in_1[15]);

  assign out_2 = in_1[7:0];
  assign out_3 = in_1[15:8];
endmodule

module AND (
  input  [15:0] in_1,
  output [7:0] out_2,
  output [7:0] out_3,
  output [7:0] out_4
);

  and and_1 (out_4[0], in_1[0], in_1[8]);
  and and_2 (out_4[1], in_1[1], in_1[9]);
  and and_3 (out_4[2], in_1[2], in_1[10]);
  and and_4 (out_4[3], in_1[3], in_1[11]);
  and and_5 (out_4[4], in_1[4], in_1[12]);
  and and_6 (out_4[5], in_1[5], in_1[13]);
  and and_7 (out_4[6], in_1[6], in_1[14]);
  and and_8 (out_4[7], in_1[7], in_1[15]);

  assign out_2 = in_1[7:0];
  assign out_3 = in_1[15:8];
endmodule

module XOR (
  input  [15:0] in_1,
  output [7:0] out_2,
  output [7:0] out_3,
  output [7:0] out_4
);

  xor xor_1 (out_4[0], in_1[0], in_1[8]);
  xor xor_2 (out_4[1], in_1[1], in_1[9]);
  xor xor_3 (out_4[2], in_1[2], in_1[10]);
  xor xor_4 (out_4[3], in_1[3], in_1[11]);
  xor xor_5 (out_4[4], in_1[4], in_1[12]);
  xor xor_6 (out_4[5], in_1[5], in_1[13]);
  xor xor_7 (out_4[6], in_1[6], in_1[14]);
  xor xor_8 (out_4[7], in_1[7], in_1[15]);

  assign out_2 = in_1[7:0];
  assign out_3 = in_1[15:8];
endmodule

module Resta (
  input  [15:0] in_1,
  output [7:0] out_2,
  output [7:0] out_3,
  output [7:0] out_4
);

  wire [7:0] not_1_out, suma_1_out_4;

  not not_1 (not_1_out[0], in_1[8]);
  not not_2 (not_1_out[1], in_1[9]);
  not not_3 (not_1_out[2], in_1[10]);
  not not_4 (not_1_out[3], in_1[11]);
  not not_5 (not_1_out[4], in_1[12]);
  not not_6 (not_1_out[5], in_1[13]);
  not not_7 (not_1_out[6], in_1[14]);
  not not_8 (not_1_out[7], in_1[15]);
  Suma suma_1 (.in_1({8'h1, not_1_out}), .out_4(suma_1_out_4));  // open: out_2, out_3
  Suma suma_2 (.in_1({suma_1_out_4, in_1[7:0]}), .out_4(out_2));  // open: out_2, out_3

  assign out_3 = in_1[7:0];
  assign out_4 = in_1[15:8];
endmodule

module NOR (
  input  [15:0] in_1,
  output [7:0] out_2,
  output [7:0] out_3,
  output [7:0] out_4
);

  nor nor_1 (out_4[0], in_1[0], in_1[8]);
  nor nor_2 (out_4[1], in_1[1], in_1[9]);
  nor nor_3 (out_4[2], in_1[2], in_1[10]);
  nor nor_4 (out_4[3], in_1[3], in_1[11]);
  nor nor_5 (out_4[4], in_1[4], in_1[12]);
  nor nor_6 (out_4[5], in_1[5], in_1[13]);
  nor nor_7 (out_4[6], in_1[6], in_1[14]);
  nor nor_8 (out_4[7], in_1[7], in_1[15]);

  assign out_2 = in_1[7:0];
  assign out_3 = in_1[15:8];
endmodule

module NAND (
  input  [15:0] in_1,
  output [7:0] out_2,
  output [7:0] out_3,
  output [7:0] out_4
);

  nand nand_1 (out_4[0], in_1[0], in_1[8]);
  nand nand_2 (out_4[1], in_1[1], in_1[9]);
  nand nand_3 (out_4[2], in_1[2], in_1[10]);
  nand nand_4 (out_4[3], in_1[3], in_1[11]);
  nand nand_5 (out_4[4], in_1[4], in_1[12]);
  nand nand_6 (out_4[5], in_1[5], in_1[13]);
  nand nand_7 (out_4[6], in_1[6], in_1[14]);
  nand nand_8 (out_4[7], in_1[7], in_1[15]);

  assign out_2 = in_1[7:0];
  assign out_3 = in_1[15:8];
endmodule

module XNOR (
  input  [15:0] in_1,
  output [7:0] out_2,
  output [7:0] out_3,
  output [7:0] out_4
);

  xnor xnor_1 (out_4[0], in_1[0], in_1[8]);
  xnor xnor_2 (out_4[1], in_1[1], in_1[9]);
  xnor xnor_3 (out_4[2], in_1[2], in_1[10]);
  xnor xnor_4 (out_4[3], in_1[3], in_1[11]);
  xnor xnor_5 (out_4[4], in_1[4], in_1[12]);
  xnor xnor_6 (out_4[5], in_1[5], in_1[13]);
  xnor xnor_7 (out_4[6], in_1[6], in_1[14]);
  xnor xnor_8 (out_4[7], in_1[7], in_1[15]);

  assign out_2 = in_1[7:0];
  assign out_3 = in_1[15:8];
endmodule

module Sumador (
  input  in_1,
  input  in_2,
  input  in_3,
  output out_4,
  output out_5
);

  wire and_1_out, and_2_out, xor_1_out;

  xor xor_1 (xor_1_out, in_1, in_2);
  and and_1 (and_1_out, in_1, in_2);
  and and_2 (and_2_out, xor_1_out, in_3);
  xor xor_2 (out_4, xor_1_out, in_3);
  or or_1 (out_5, and_2_out, and_1_out);
endmodule
